# Fritzing sketch PIR (saved by Fritzing 0.8.7b)
breadboards: 1

parts:
  S1 = PIR2 [package=THT]
  LED1 = LED - 5mm [color="Red (633nm)" package="5 mm [THT]"]
  R1 = Resistor [tolerance=±5% resistance=220 package=THT]
  元件1 = Sunfounder Mega 2560 (Rev3)

nets:
  GND: S1.GND, LED1.cathode, 元件1.GND
  N1: S1.OUT, 元件1.D11_PWM
  VCC: S1.VCC, 元件1.5V
  N2: LED1.anode, R1.Pin_0
  N3: R1.Pin_1, 元件1.D36

notes:
  PIR

custom parts:
  Sunfounder Mega 2560 (Rev3): The Arduino Mega 2560 is a microcontroller board based on the ATmega2560 (datasheet). It has 54 digital input/output pins (of which 14 can be used as PWM outputs), 16 analog inputs, 4 UARTs (hardware serial ports), a 16 MHz crystal oscillator, a USB connection, a power jack, an ICSP header, and a reset button. It contains everything needed to support the microcontroller; simply connect it to a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
