# Fritzing sketch BMP280_I2C (saved by Fritzing 0.8.7b)
breadboards: 1

parts:
  U1 = BMP280 Module [package="DIP7 [THT]"]
  元件2 = Sunfounder Mega 2560 (Rev3)

nets:
  3.3V: U1.3.3V, 元件2.3V3
  GND: U1.GND, 元件2.GND
  N1: U1.SCK, 元件2.D21/SCL
  N2: U1.SDO, 元件2.D20/SDA

custom parts:
  BMP280 Module: The BMP280 is an absolute barometric pressure sensor especially designed for mobile applications. The sensor module is housed in an extremely compact 8-pin metal-lid LGA package with a footprint of only 2.0 × 2.5 mm2 and 0.95 mm package height. Its small dimensions and its low power consumption of 2.7 µA @1Hz allow the implementation in battery driven devices such as mobile phones, GPS modules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
  Sunfounder Mega 2560 (Rev3): The Arduino Mega 2560 is a microcontroller board based on the ATmega2560 (datasheet). It has 54 digital input/output pins (of which 14 can be used as PWM outputs), 16 analog inputs, 4 UARTs (hardware serial ports), a 16 MHz crystal oscillator, a USB connection, a power jack, an ICSP header, and a reset button. It contains everything needed to support the microcontroller; simply connect it to a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
