# Fritzing sketch BMP180 (saved by Fritzing 0.8.7b)

parts:
  元件1 = Sunfounder Mega 2560 (Rev3)
  module1 = Barometer

nets:
  N1: 元件1.D21/SCL, module1.SCL
  N2: 元件1.D20/SDA, module1.SDA
  5V: 元件1.5V, module1.VCC
  GND: 元件1.GND, module1.GND

notes:
  BMP180

custom parts:
  Sunfounder Mega 2560 (Rev3): The Arduino Mega 2560 is a microcontroller board based on the ATmega2560 (datasheet). It has 54 digital input/output pins (of which 14 can be used as PWM outputs), 16 analog inputs, 4 UARTs (hardware serial ports), a 16 MHz crystal oscillator, a USB connection, a power jack, an ICSP header, and a reset button. It contains everything needed to support the microcontroller; simply connect it to a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
  Barometer: barometer module of SunFounder Sensor Kit
