# Fritzing sketch rfid (saved by Fritzing 0.8.7b)
breadboards: 1

parts:
  module1 = RFID-RC522
  元件1 = Sunfounder Mega 2560 (Rev3)
  C1 = Ceramic Capacitor [capacitance=100nF package="200 mil [THT, multilayer]"]

nets:
  VCC: module1.VCC, 元件1.3V3, C1.0
  N1: module1.RST, 元件1.D2_PWM
  GND: module1.GND, 元件1.GND, C1.1
  N2: module1.MISO, 元件1.D3_PWM
  N3: module1.MOSI, 元件1.D4_PWM
  N4: module1.SCK, 元件1.D5_PWM
  N5: module1.NSS, 元件1.D6_PWM
  N6: module1.IRQ, 元件1.D7_PWM

custom parts:
  RFID-RC522: RFID-RC522 module from Sunfounder
  Sunfounder Mega 2560 (Rev3): The Arduino Mega 2560 is a microcontroller board based on the ATmega2560 (datasheet). It has 54 digital input/output pins (of which 14 can be used as PWM outputs), 16 analog inputs, 4 UARTs (hardware serial ports), a 16 MHz crystal oscillator, a USB connection, a power jack, an ICSP header, and a reset button. It contains everything needed to support the microcontroller; simply connect it to a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
