# Fritzing sketch Nano-nrf24l01 (saved by Fritzing 0.8.7b)

parts:
  元件1 = SunFounder Nano (V4.0) [part_number="SunFounder Nano (V4.0) "]
  U1 = nRF24L01 [package="DIP8 [THT]"]
  元件2 = 4-Channels Relay

nets:
  GND: 元件1.GND, U1.connector0, 元件2.GND
  N1: 元件1.D3, 元件2.IN4
  N2: 元件1.D4, 元件2.IN3
  N3: 元件1.D5, 元件2.IN2
  N4: 元件1.D6, 元件2.IN1
  N5: 元件1.D8, U1.connector2
  N6: 元件1.D9, U1.connector3
  N7: 元件1.D10, U1.connector4
  N8: 元件1.D11/MOSI, U1.connector5
  N9: 元件1.D12/MISO, U1.connector6
  5V: 元件1.5V, 元件2.VCC
  N10: 元件1.3V3, U1.connector1
  N11: 元件1.D13/SCK, U1.connector7

notes:
  4-Channel Relay Module
  SunFounder Nano
  nRF24L01

custom parts:
  SunFounder Nano (V4.0): Our Nano is fully compatible with Arduino Nano,but the driver of Sunfounder Nano is PL2303
  nRF24L01: nrf24l01 wireless module
