# Fritzing sketch mega2560-NRF24L01 (saved by Fritzing 0.8.7b)
breadboards: 1

parts:
  元件1 = Sunfounder Mega 2560 (Rev3)
  S1 = Pushbutton [package="[THT]"]
  S2 = Pushbutton [package="[THT]"]
  S3 = Pushbutton [package="[THT]"]
  S4 = Pushbutton [package="[THT]"]
  S5 = Pushbutton [package="[THT]"]
  U1 = nRF24L01 [package="DIP8 [THT]"]

nets:
  N1: 元件1.GND, S1.Pin_3, S1.Pin_4, S2.Pin_3, S2.Pin_4, S3.Pin_3, S3.Pin_4, S4.Pin_3, S4.Pin_4, S5.Pin_3, S5.Pin_4, U1.connector0
  N2: 元件1.3V3, U1.connector1
  N3: 元件1.D2_PWM, S5.Pin_1, S5.Pin_2
  N4: 元件1.D3_PWM, S4.Pin_1, S4.Pin_2
  N5: 元件1.D4_PWM, S3.Pin_1, S3.Pin_2
  N6: 元件1.D5_PWM, S2.Pin_1, S2.Pin_2
  N7: 元件1.D6_PWM, S1.Pin_1, S1.Pin_2
  N8: 元件1.D22, U1.connector2
  N9: 元件1.D24, U1.connector3
  N10: 元件1.D26, U1.connector4
  N11: 元件1.D28, U1.connector5
  N12: 元件1.D30, U1.connector6
  N13: 元件1.D32, U1.connector7

notes:
  nRF24L01
  sw1
  sw2
  sw3
  sw4
  sw5

custom parts:
  Sunfounder Mega 2560 (Rev3): The Arduino Mega 2560 is a microcontroller board based on the ATmega2560 (datasheet). It has 54 digital input/output pins (of which 14 can be used as PWM outputs), 16 analog inputs, 4 UARTs (hardware serial ports), a 16 MHz crystal oscillator, a USB connection, a power jack, an ICSP header, and a reset button. It contains everything needed to support the microcontroller; simply connect it to a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
  nRF24L01: nrf24l01 wireless module
