# Fritzing sketch Acquisition board (saved by Fritzing 0.8.7b)
breadboards: 1

parts:
  module1 = Photoresistor
  module2 = MQ-2 Gas Sensor
  U1 = nRF24L01 [package="DIP8 [THT]"]
  module3 = RFID-RC522
  S1 = PIR2 [package=THT]
  R1 = Resistor [tolerance=±5% resistance=220 package=THT]
  LED1 = LED - 5mm [color="Red (633nm)" package="5 mm [THT]"]
  LED2 = LED - 5mm [color="Red (635nm)" package="5 mm [THT]"]
  元件1 = Sunfounder Mega 2560+W5100
  module5 = DHT11 Humiture Sensor
  R2 = Resistor [tolerance=±5% resistance=220 package=THT]
  U2 = BMP280 Module [package="DIP7 [THT]"]

nets:
  N1: module1.SIG, 元件1.A0
  GND: module1.GND, module2.GND, U1.connector0, module3.GND, S1.GND, LED1.cathode, LED2.cathode, 元件1.GND, module5.GND, U2.GND
  VCC: module1.VCC, module2.VCC, S1.VCC, 元件1.5V, module5.VCC, U2.VCC
  N2: module2.AO, 元件1.A1
  VCC_2: U1.connector1, module3.VCC, 元件1.3V3
  N3: U1.connector2, 元件1.D22
  N4: U1.connector3, 元件1.D24
  N5: U1.connector4, 元件1.D26
  N6: U1.connector5, 元件1.D28
  N7: U1.connector6, 元件1.D30
  N8: U1.connector7, 元件1.D32
  N9: module3.RST, 元件1.D2_PWM
  N10: module3.MISO, 元件1.D3_PWM
  N11: module3.MOSI, 元件1.D4_PWM
  N12: module3.SCK, 元件1.D5_PWM
  N13: module3.NSS, 元件1.D6_PWM
  N14: module3.IRQ, 元件1.D7_PWM
  N15: S1.OUT, 元件1.D36
  N16: R1.Pin_0, LED1.anode
  N17: R1.Pin_1, 元件1.D40
  N18: LED2.anode, R2.Pin_0
  N19: 元件1.D21/SCL, U2.SCK
  N20: 元件1.D20/SDA, U2.SDI
  N21: 元件1.D34, module5.SIG
  N22: 元件1.D38, R2.Pin_1

notes:
  NRF24L01
  BMP280
  PIR
  Photoresistor
  DHT11
  MQ-2
  RFID
  Mega 2560+w5100

custom parts:
  Photoresistor: Photoresistor module of SunFounder Sensor Kit
  MQ-2 Gas Sensor: MQ-2 Gas Sensor module of SunFounder Sensor Kit
  nRF24L01: nrf24l01 wireless module
  RFID-RC522: RFID-RC522 module from Sunfounder
  DHT11 Humiture Sensor: DHT11 Humiture Sensor module of SunFounder Sensor Kit
  BMP280 Module: The BMP280 is an absolute barometric pressure sensor especially designed for mobile applications. The sensor module is housed in an extremely compact 8-pin metal-lid LGA package with a footprint of only 2.0 × 2.5 mm2 and 0.95 mm package height. Its small dimensions and its low power consumption of 2.7 µA @1Hz allow the implementation in battery driven devices such as mobile phones, GPS modules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
