# Fritzing sketch Acquisition board (saved by Fritzing 0.8.7b)
breadboards: 1

parts:
  module1 = Photoresistor
  module2 = MQ-2 Gas Sensor
  U1 = nRF24L01 [package="DIP8 [THT]"]
  module3 = RFID-RC522
  module4 = Barometer
  S1 = PIR2 [package=THT]
  R1 = Resistor [tolerance=±5% resistance=220 package=THT]
  LED1 = LED - 5mm [color="Red (633nm)" package="5 mm [THT]"]
  LED2 = LED - 5mm [color="Red (635nm)" package="5 mm [THT]"]
  元件1 = Sunfounder Mega 2560+W5100
  module5 = DHT11 Humiture Sensor
  R2 = Resistor [tolerance=±5% resistance=220 package=THT]

nets:
  N1: module1.SIG, 元件1.A0
  GND: module1.GND, module2.GND, U1.connector0, module3.GND, module4.GND, S1.GND, LED1.cathode, LED2.cathode, 元件1.GND, module5.GND
  VCC: module1.VCC, module2.VCC, module4.VCC, S1.VCC, 元件1.5V, module5.VCC
  N2: module2.AO, 元件1.A1
  VCC_2: U1.connector1, module3.VCC, 元件1.3V3
  N3: U1.connector2, 元件1.D22
  N4: U1.connector3, 元件1.D24
  N5: U1.connector4, 元件1.D26
  N6: U1.connector5, 元件1.D28
  N7: U1.connector6, 元件1.D30
  N8: U1.connector7, 元件1.D32
  N9: module3.RST, 元件1.D2_PWM
  N10: module3.MISO, 元件1.D3_PWM
  N11: module3.MOSI, 元件1.D4_PWM
  N12: module3.SCK, 元件1.D5_PWM
  N13: module3.NSS, 元件1.D6_PWM
  N14: module3.IRQ, 元件1.D7_PWM
  N15: module4.SCL, 元件1.D21/SCL
  N16: module4.SDA, 元件1.D20/SDA
  N17: S1.OUT, 元件1.D36
  N18: R1.Pin_0, LED1.anode
  N19: R1.Pin_1, 元件1.D40
  N20: LED2.anode, R2.Pin_0
  N21: 元件1.D34, module5.SIG
  N22: 元件1.D38, R2.Pin_1

notes:
  NRF24L01
  BMP180
  PIR
  Photoresistor
  DHT11
  MQ-2
  RFID
  Mega 2560+w5100

custom parts:
  Photoresistor: Photoresistor module of SunFounder Sensor Kit
  MQ-2 Gas Sensor: MQ-2 Gas Sensor module of SunFounder Sensor Kit
  nRF24L01: nrf24l01 wireless module
  RFID-RC522: RFID-RC522 module from Sunfounder
  Barometer: barometer module of SunFounder Sensor Kit
  DHT11 Humiture Sensor: DHT11 Humiture Sensor module of SunFounder Sensor Kit
